// Digital circuit play_with_digital.dig as structural Verilog
module play_with_digital (
  input  in_1,
  input  in_2,
  input  in_3,
  input  in_4,
  input  in_5,
  input  in_6,
  input  in_9,
  output out_7,
  output out_8,
  output out_10
);

  wire and_2_out, or_1_out;

  xor xor_1 (out_7, in_5, in_6);
  and and_1 (out_8, in_5, in_6);
  and and_2 (and_2_out, in_1, in_2);
  or or_1 (or_1_out, in_4, in_3);
  nand nand_1 (out_10, in_9, out_10);
  LED led_1 (.in(and_2_out));
  LED led_2 (.in(or_1_out));

  // Notes on the sheet:
  //   x
  //   y
endmodule
