// Digital circuit play_with_digital_2_with_java_8.dig as structural Verilog
module play_with_digital_2_with_java_8 (
  input  in_1,
  input  in_2,
  output out_3
);

  xor xor_1 (out_3, in_1, in_2);
endmodule
